// Logisim project ARM_CPU.circ as structural Verilog
module main (
);

  FD fd_1 ();
  Fetch fetch_1 ();
  Decode decode_1 ();
  DE de_1 ();
  Execute execute_1 ();
  EM em_1 ();
  MW mw_1 ();
  Memory memory_1 ();
endmodule
